# Fritzing sketch VoiceModulator (saved by Fritzing 0.9.3b)
breadboards: 1

parts:
  Part2 = TRRS 3.5mm Jack Breakout
  Part1 = Arduino Mega 2560 (Rev3)
  Part3 = OLED Monochrome 128x64 1.3 inch [part_number=938]
  Keypad4x1 = Keypad Membran 4x4
  Part4 = Adafruit MAX9814 Electret Microphone Amplifier [part_number="Adafruit #1713"]
  U1 = POT [package=pot_alpha_rv16af-20]
  C1 = Electrolytic Capacitor [capacitance=100μF package="0807 [SMD, electrolytic]"]
  R1 = Resistor [tolerance=±5% resistance=10k package=THT]
  R2 = Resistor [tolerance=±5% resistance=220 package=THT]
  C2 = Electrolytic Capacitor [capacitance=10µF package="100 mil [THT, electrolytic]"]

nets:
  GND: Part2.SLEEVE, Part1.GND, Part3.GND, Part4.GND, R1.Pin_1, C2.+
  N1: Part2.RING2, Part2.RING1, Part2.TIP, U1.E
  N2: Part1.A0, C1.+, R1.Pin_0
  N3: Part1.D21/SCL, Part3.SCLK_SCK
  N4: Part1.D20/SDA, Part3.MOSI_SDA
  N5: Part1.D9_PWM, U1.S, C2.-
  5V: Part1.5V, Part3.VIN, R2.Pin_0
  N6: Part1.D4_PWM, Part3.RESET
  N7: Part1.D24, Keypad4x1.Pin1
  N8: Part1.D26, Keypad4x1.Pin2
  N9: Part1.D28, Keypad4x1.Pin3
  N10: Part1.D30, Keypad4x1.Pin4
  N11: Part1.D32, Keypad4x1.Pin5
  N12: Part1.D34, Keypad4x1.Pin6
  N13: Part1.D36, Keypad4x1.Pin7
  N14: Part1.D38, Keypad4x1.Pin8
  N15: Part4.VDD, Part4.GAIN
  N16: Part4.OUTPUT, C1.-, R2.Pin_1

custom parts:
  OLED Monochrome 128x64 1.3 inch: These displays are small, only about 1.3" diagonal, but very readable due to the high contrast of an OLED display. This display is made of 128x64 individual white OLED pixels, each one is turned on or off by the controller chip. Because the display makes its own light, no backlight is required. This reduces the power required to run the OLED and is why the display has such high contrast; we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
  Keypad Membran 4x4: Membrane Keypad 4x4 Matrix
  Adafruit MAX9814 Electret Microphone Amplifier: Add an ear to your project with this well-designed electret microphone amplifier with AGC. This fully assembled and tested board comes with a 20-20KHz electret microphone soldered on. For the amplification, we use the Maxim MAX9814, a specialty chip that is designed for amplifying electret microphones in situations where the loudness of the audio isn't predictable. This fancy microphone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
